# Fritzing sketch CanSat (saved by Fritzing 1.0.1rc)
circuit board: 7.21687cm x 3.02552cm
breadboards: 1

parts:
  Pico_H1 = Raspberry Pi Pico H
  BMP280_Breakout2 = BMP280 Breakout Board [part_number=BMP280]
  Part1 = Adafruit RFM9x LoRa Radio [part_number="Adafruit #3072 and #3073"]
  Part2 = Adafruit Ultimate GPS v3 [part_number="Adafruit #746"]
  Part3 = Adafruit BNO085 9-DOF Orientation IMU Fusion [part_number="Addfruit #4754"]

nets:
  GND: Pico_H1.GND, BMP280_Breakout2.GND, Part1.GND, Part2.GND, Part3.GND
  VCC: Pico_H1.3V3, BMP280_Breakout2.VCC, Part1.VIN, Part2.VIN, Part3.VCC
  N1: Pico_H1.GP28_A2, Part1.MISO
  N2: Pico_H1.GP27_A1, Part1.MOSI
  N3: Pico_H1.GP26_A0, Part1.SCK
  N4: Pico_H1.GP22, Part1.CS
  N5: Pico_H1.GP21, Part1.RST
  N6: Pico_H1.GP19, BMP280_Breakout2.SCL, Part3.SCL/SCK/RX
  N7: Pico_H1.GP18, BMP280_Breakout2.SDA, Part3.SDA/MISO/TX
  N8: Pico_H1.GP1, Part2.TX
  N9: Pico_H1.GP0, Part2.RX

notes:
  CanSat

custom parts:
  Raspberry Pi Pico H: Raspberry Pi Pico H. Based around the RP2040 microcontroller the Pico H is a low cost microcontroller device bringing Raspberry Pi quality, cost, and easy of use to the microcontroller space.
  BMP280 Breakout Board: A fast and precise environmental sensor that can measure temperature, pressure, and altitude. Our BMP280 breakout is Raspberry-Pi and Arduino-compatible.
  Adafruit RFM9x LoRa Radio: Sending data over long distances is like magic, and now you can be a magician with this range of powerful and easy-to-use radio modules. Sure, sometimes you want to talk to a computer (a good time to use WiFi) or perhaps communicate with a Phone (choose Bluetooth Low Energy!) but what if you want to send data very far? Most WiFi, Bluetooth, Zigbee and other wireless chipsets use 2.4GHz, which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
  Adafruit Ultimate GPS v3: We carry a few different GPS modules here in the Adafruit shop, but none that satisfied our every desire - that's why we designed this little GPS breakout board. We believe this is the Ultimate GPS module, so we named it that. It's got everything you want and more: -165 dBm sensitivity, 10 Hz updates, 66 channels 5V friendly design and only 20mA current draw Breadboard friendly + two mounting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
